// Logisim project fpadder.circ as structural Verilog: 1 circuit, main circuit main
module main (
  input  Big_ALU,
  input  [15:0] in_2,
  input  [15:0] in_3,
  input  in_4,
  input  [3:0] in_5,
  input  [3:0] in_6,
  input  in_7,
  input  in_8,
  input  in_9,
  input  in_10,
  output [15:0] out_11,
  output out_12,
  output [3:0] _2_s_compliment,
  output [3:0] out_14,
  output [15:0] out_15,
  output [3:0] out_16,
  output out_17
);

  wire adder_6_cout, and_1_out, and_2_out, and_4_out, and_5_out, and_6_out, bitselector_1_out,
       bitselector_2_out, bitselector_3_out, bitselector_4_out, comparator_1_gt, multiplexer_6_out,
       multiplexer_11_out, not_1_out, not_2_out, not_3_out, not_4_out, or_4_out, subtractor_1_bout, xor_1_out;
  wire [3:0] adder_5_out, bitfinder_1_index, multiplexer_1_out, multiplexer_4_out, multiplexer_10_out,
       multiplexer_13_out, multiplexer_14_out, subtractor_1_out, subtractor_3_out;
  wire [15:0] adder_2_out, adder_3_out, adder_4_out, adder_6_out, multiplexer_2_out, multiplexer_3_out,
       multiplexer_5_out, multiplexer_8_out, multiplexer_12_out, multiplexer_15_out, or_1_out, or_2_out,
       or_3_out, register_1_q, shifter_1_out, shifter_2_out, shifter_3_out, shifter_4_out, shifter_5_out,
       xor_3_out, xor_4_out;

  Subtractor #(.width(4)) subtractor_1 (
    .a(in_5), .b(in_6), .out(subtractor_1_out), .bin(in_4), .bout(subtractor_1_bout));
  xor xor_1 (xor_1_out, in_9, in_10);
  Shifter #(.width(16), .shift("lr")) shifter_1 (.in(in_2), .\dist (4'b0001), .out(shifter_1_out));
  Shifter #(.width(16), .shift("lr")) shifter_2 (.in(in_3), .\dist (4'b0001), .out(shifter_2_out));
  assign _2_s_compliment = subtractor_1_out ^ 4'b1111;  // XOR_Gate xor_2, 4 bits wide
  Multiplexer #(.width(4)) multiplexer_1 (
    .in0(in_5), .in1(in_6), .out(multiplexer_1_out), .sel(subtractor_1_bout), .en(in_8));
  assign or_1_out = shifter_1_out | 16'h8000;  // OR_Gate or_1, 16 bits wide
  assign or_2_out = shifter_2_out | 16'h8000;  // OR_Gate or_2, 16 bits wide
  Adder #(.width(4)) adder_1 (.a(_2_s_compliment), .b(4'b0001), .out(out_14));  // open: cin, cout
  Multiplexer #(.width(16)) multiplexer_2 (
    .in0(or_1_out), .in1(or_2_out), .out(multiplexer_2_out), .sel(not_2_out), .en(in_8));
  not not_1 (not_1_out, not_2_out);
  not not_2 (not_2_out, subtractor_1_bout);
  Multiplexer #(.width(16)) multiplexer_3 (
    .in0(or_1_out), .in1(or_2_out), .out(multiplexer_3_out), .sel(not_1_out), .en(in_8));
  Multiplexer #(.width(4)) multiplexer_4 (
    .in0(subtractor_1_out), .in1(out_14), .out(multiplexer_4_out), .sel(subtractor_1_bout), .en(in_8));
  Shifter #(.width(16), .shift("lr")) shifter_3 (
    .in(multiplexer_2_out), .\dist (multiplexer_4_out), .out(shifter_3_out));
  assign xor_3_out = shifter_3_out ^ {16{1'b1}};  // XOR_Gate xor_3, 16 bits wide
  Adder #(.width(16)) adder_2 (.a(xor_3_out), .b(16'h1), .out(adder_2_out));  // open: cin, cout
  Multiplexer #(.width(16)) multiplexer_5 (
    .in0(shifter_3_out), .in1(adder_2_out), .out(multiplexer_5_out), .sel(xor_1_out), .en(in_8));
  Adder #(.width(16)) adder_3 (
    .a(multiplexer_3_out), .b(multiplexer_5_out), .out(adder_3_out), .cout(out_12));  // open: cin
  Comparator #(.width(16), .mode("unsigned")) comparator_1 (
    .a(multiplexer_3_out), .b(shifter_3_out), .gt(comparator_1_gt));  // open: eq, lt
  not not_3 (not_3_out, xor_1_out);
  not not_4 (not_4_out, comparator_1_gt);
  and and_1 (and_1_out, out_12, not_3_out);
  Multiplexer multiplexer_6 (.in0(in_9), .in1(in_10), .out(multiplexer_6_out), .sel(not_4_out), .en(in_8));
  assign xor_4_out = adder_3_out ^ {16{1'b1}};  // XOR_Gate xor_4, 16 bits wide
  Adder #(.width(16)) adder_4 (.a(xor_4_out), .b(16'h1), .out(adder_4_out));  // open: cin, cout
  and and_2 (and_2_out, not_4_out, xor_1_out);
  Multiplexer multiplexer_7 (.in0(in_9), .in1(multiplexer_6_out), .out(out_17), .sel(xor_1_out), .en(in_8));
  Multiplexer #(.width(16)) multiplexer_8 (
    .in0(adder_3_out), .in1(adder_4_out), .out(multiplexer_8_out), .sel(and_2_out), .en(in_8));
  Multiplexer #(.width(16), .enable("false")) multiplexer_9 (
    .in0(multiplexer_8_out), .in1(register_1_q), .out(out_11), .sel(in_7));
  Multiplexer #(.width(4)) multiplexer_10 (
    .in0(4'b0000), .in1(4'b0001), .out(multiplexer_10_out), .sel(multiplexer_11_out), .en(in_8));
  Multiplexer #(.enable("false")) multiplexer_11 (.in0(and_1_out), .in1(in_7), .out(multiplexer_11_out), .sel(in_7));
  Shifter #(.width(16), .shift("lr")) shifter_4 (.in(out_11), .\dist (multiplexer_10_out), .out(shifter_4_out));
  Multiplexer #(.width(16)) multiplexer_12 (
    .in0({16{1'b0}}), .in1(16'h8000), .out(multiplexer_12_out), .sel(multiplexer_11_out), .en(in_8));
  assign or_3_out = shifter_4_out | multiplexer_12_out;  // OR_Gate or_3, 16 bits wide
  Multiplexer #(.width(4)) multiplexer_13 (
    .in0(4'b0000), .in1(4'b0001), .out(multiplexer_13_out), .sel(multiplexer_11_out), .en(in_8));
  Multiplexer #(.width(4), .enable("false")) multiplexer_14 (
    .in0(multiplexer_1_out), .in1(out_16), .out(multiplexer_14_out), .sel(in_7));
  Adder #(.width(4)) adder_5 (.a(multiplexer_13_out), .b(multiplexer_14_out), .out(adder_5_out));  // open: cin, cout
  BitFinder #(.width(16), .\type ("high1")) bitfinder_1 (.in(or_3_out), .index(bitfinder_1_index));  // open: found
  Shifter #(.width(16)) shifter_5 (.in(or_3_out), .\dist (subtractor_3_out), .out(shifter_5_out));
  Subtractor #(.width(4)) subtractor_2 (.a(adder_5_out), .b(subtractor_3_out), .out(out_16));  // open: bin, bout
  Subtractor #(.width(4)) subtractor_3 (.a(4'b1111), .b(bitfinder_1_index), .out(subtractor_3_out));  // open: bin, bout
  Adder #(.width(16)) adder_6 (.a(shifter_5_out), .b(16'h10), .out(adder_6_out), .cout(adder_6_cout));  // open: cin
  Multiplexer #(.width(16)) multiplexer_15 (
    .in0(shifter_5_out), .in1(adder_6_out), .out(multiplexer_15_out), .sel(or_4_out), .en(in_8));
  and and_3 (in_7, or_4_out, adder_6_cout);
  BitSelector #(.width(16)) bitselector_1 (.in(shifter_5_out), .out(bitselector_1_out), .sel(4'b0100));
  BitSelector #(.width(16)) bitselector_2 (.in(shifter_5_out), .out(bitselector_2_out), .sel(4'b0011));
  BitSelector #(.width(16)) bitselector_3 (.in(shifter_5_out), .out(bitselector_3_out), .sel(4'b0010));
  BitSelector #(.width(16)) bitselector_4 (.in(shifter_5_out), .out(bitselector_4_out), .sel(4'b0001));
  Register #(.width(16), .trigger("high")) register_1 (
    .D(multiplexer_15_out), .en(in_7), .Q(register_1_q));  // open: clk, clr
  and and_4 (and_4_out, bitselector_1_out, bitselector_2_out);
  and and_5 (and_5_out, bitselector_2_out, bitselector_4_out);
  and and_6 (and_6_out, bitselector_2_out, bitselector_3_out);
  Shifter #(.width(16)) shifter_6 (.in(multiplexer_15_out), .\dist (4'b0001), .out(out_15));
  or or_4 (or_4_out, and_4_out, and_5_out, and_6_out);

  // Notes on the sheet:
  //                       Exponents
  //   Right shift
  //   1's compliment
  //   Adding significand
  //   Exponent diff
  //   Pre result exp
  //   Shift right
  //   Control for small exp
  //   2's complement
  //   A
  //   B
  //   Sign selection
  //   Shifting right
  //   Inc exp
  //   Dec exp
  //   Shifting left
  //   Rounding
  //   G-1
  //   G
  //   R
  //   S
  //   Shift left
endmodule
